# Fritzing sketch arduino (saved by Fritzing 1.0.3b)
breadboards: 1

parts:
  Bauteil1 = Arduino Uno (Rev3)
  R1 = Resistor [tolerance=±5% power=0.25W resistance=220 package=THT]
  DME_Station_Relaiskontakt = TILT-SWITCH-SW-200D [package=reed_switch_plastic]
  R2 = Resistor [tolerance=±5% power=0.25W resistance=220 package=THT]
  Mod1 = Amica NodeMCU DEVKIT 1.0
  LED_Strip_1 = WS2812 RGB LED strip

nets:
  N1: Bauteil1.D8, R2.Pin_0
  N2: Bauteil1.D0/RX, Mod1.pin3
  N3: Bauteil1.D1/TX, Mod1.pin4
  N4: Bauteil1.D7, R1.Pin_1, DME_Station_Relaiskontakt.2
  5V: Bauteil1.5V, DME_Station_Relaiskontakt.1, LED_Strip_1.VCC
  GND: Bauteil1.GND, R1.Pin_0, LED_Strip_1.GND
  N5: R2.Pin_1, LED_Strip_1.DIN

custom parts:
  WS2812 RGB LED strip: WS2812 strip
